// Logisim project LC-3 (1).circ as structural Verilog: 13 circuits, main circuit SignExtent6
module _18BitALU (
  input  [17:0] Input_1,
  input  [1:0] ALUSelect,
  input  [17:0] Input_2,
  output cout,
  output [17:0] out_5,
  output ZF,
  output CF
);

  wire [17:0] and_1_out, n18bitadder_1_out_4, nand_1_out, nor_1_out, substractor_1_out_3;

  _18BitAdder u_18bitadder_1 (.cin(1'b0), .A(Input_1), .B(Input_2), .cout(cout), .out_4(n18bitadder_1_out_4));
  assign and_1_out = Input_1 & Input_2;  // AND_Gate and_1, 18 bits wide
  Substractor substractor_1 (.in_1(Input_1), .in_2(Input_2), .out_3(substractor_1_out_3), .CF(CF));
  assign nand_1_out = ~(Input_1 & Input_2);  // NAND_Gate nand_1, 18 bits wide
  assign nor_1_out = ~(Input_1 | Input_2);  // NOR_Gate nor_1, 18 bits wide
  _18BitNORGate u_18bitnorgate_1 (.in_1(substractor_1_out_3), .out_2(ZF));
  Multiplexer #(.select(2), .width(18), .enable("false")) multiplexer_1 (
    .in0(n18bitadder_1_out_4), .in1(and_1_out), .in2(nand_1_out), .in3(nor_1_out), .out(out_5),
    .sel(ALUSelect));
endmodule

module PC18 (
  input  write,
  input  [17:0] \input ,
  input  en,
  input  clk,
  output [17:0] \output 
);

  wire [17:0] multiplexer_1_out;

  Multiplexer #(.width(18), .enable("false")) multiplexer_1 (
    .in0(\output ), .in1(\input ), .out(multiplexer_1_out), .sel(write));
  Register #(.width(18)) register_1 (.D(multiplexer_1_out), .en(en), .Q(\output ), .clk(clk), .clr(1'b0));
endmodule

// Read Register 1
module _18BitRegisterFile (
  input  [3:0] Read_Register_1,
  input  [3:0] Read_Register_1_2,
  input  [3:0] Write_Register_1,
  input  [17:0] in_4,
  input  clk,
  input  writeEnable,
  output [17:0] Register_1_Output,
  output [17:0] Register_2_Output
);

  wire and_1_out, and_2_out, and_3_out, and_4_out, and_5_out, and_6_out, and_7_out, and_8_out, and_9_out,
       and_10_out, and_11_out, and_12_out, and_13_out, and_14_out, and_15_out, and_16_out, decoder_1_out0,
       decoder_1_out1, decoder_1_out2, decoder_1_out3, decoder_1_out4, decoder_1_out5, decoder_1_out6,
       decoder_1_out7, decoder_1_out8, decoder_1_out9, decoder_1_out10, decoder_1_out11, decoder_1_out12,
       decoder_1_out13, decoder_1_out14, decoder_1_out15, decoder_2_out0, decoder_2_out1, decoder_2_out2,
       decoder_2_out3, decoder_2_out4, decoder_2_out5, decoder_2_out6, decoder_2_out7, decoder_2_out8,
       decoder_2_out9, decoder_2_out10, decoder_2_out11, decoder_2_out12, decoder_2_out13, decoder_2_out14,
       decoder_2_out15, decoder_3_out0, decoder_3_out1, decoder_3_out2, decoder_3_out3, decoder_3_out4,
       decoder_3_out5, decoder_3_out6, decoder_3_out7, decoder_3_out8, decoder_3_out9, decoder_3_out10,
       decoder_3_out11, decoder_3_out12, decoder_3_out13, decoder_3_out14, decoder_3_out15;
  wire [17:0] n18bitregister_1_output, n18bitregister_2_output, n18bitregister_3_output,
       n18bitregister_4_output, n18bitregister_5_output, n18bitregister_6_output, n18bitregister_7_output,
       n18bitregister_8_output, n18bitregister_9_output, n18bitregister_10_output, n18bitregister_11_output,
       n18bitregister_12_output, n18bitregister_13_output, n18bitregister_14_output,
       n18bitregister_15_output, n18bitregister_16_output;

  Decoder #(.select(4), .enable("false")) decoder_1 (
    .out0(decoder_1_out0), .out1(decoder_1_out1), .out2(decoder_1_out2), .out3(decoder_1_out3),
    .out4(decoder_1_out4), .out5(decoder_1_out5), .out6(decoder_1_out6), .out7(decoder_1_out7),
    .out8(decoder_1_out8), .out9(decoder_1_out9), .out10(decoder_1_out10), .out11(decoder_1_out11),
    .out12(decoder_1_out12), .out13(decoder_1_out13), .out14(decoder_1_out14), .out15(decoder_1_out15),
    .sel(Read_Register_1_2));
  Decoder #(.select(4), .enable("false")) decoder_2 (
    .out0(decoder_2_out0), .out1(decoder_2_out1), .out2(decoder_2_out2), .out3(decoder_2_out3),
    .out4(decoder_2_out4), .out5(decoder_2_out5), .out6(decoder_2_out6), .out7(decoder_2_out7),
    .out8(decoder_2_out8), .out9(decoder_2_out9), .out10(decoder_2_out10), .out11(decoder_2_out11),
    .out12(decoder_2_out12), .out13(decoder_2_out13), .out14(decoder_2_out14), .out15(decoder_2_out15),
    .sel(Write_Register_1));
  and and_1 (and_1_out, decoder_2_out14, writeEnable);
  and and_2 (and_2_out, decoder_2_out15, writeEnable);
  and and_3 (and_3_out, decoder_2_out10, writeEnable);
  and and_4 (and_4_out, decoder_2_out11, writeEnable);
  and and_5 (and_5_out, decoder_2_out12, writeEnable);
  and and_6 (and_6_out, decoder_2_out13, writeEnable);
  and and_7 (and_7_out, decoder_2_out8, writeEnable);
  and and_8 (and_8_out, decoder_2_out9, writeEnable);
  and and_9 (and_9_out, decoder_2_out5, writeEnable);
  and and_10 (and_10_out, decoder_2_out6, writeEnable);
  and and_11 (and_11_out, decoder_2_out7, writeEnable);
  and and_12 (and_12_out, decoder_2_out0, writeEnable);
  and and_13 (and_13_out, decoder_2_out1, writeEnable);
  and and_14 (and_14_out, decoder_2_out2, writeEnable);
  and and_15 (and_15_out, decoder_2_out3, writeEnable);
  Decoder #(.select(4), .enable("false")) decoder_3 (
    .out0(decoder_3_out0), .out1(decoder_3_out1), .out2(decoder_3_out2), .out3(decoder_3_out3),
    .out4(decoder_3_out4), .out5(decoder_3_out5), .out6(decoder_3_out6), .out7(decoder_3_out7),
    .out8(decoder_3_out8), .out9(decoder_3_out9), .out10(decoder_3_out10), .out11(decoder_3_out11),
    .out12(decoder_3_out12), .out13(decoder_3_out13), .out14(decoder_3_out14), .out15(decoder_3_out15),
    .sel(Read_Register_1));
  and and_16 (and_16_out, decoder_2_out4, writeEnable);
  _18BitRegister u_18bitregister_1 (
    .\input (in_4), .clock(clk), .\output (n18bitregister_1_output), .enable(and_12_out));
  _18BitRegister u_18bitregister_2 (
    .\input (in_4), .clock(clk), .\output (n18bitregister_2_output), .enable(and_13_out));
  _18BitRegister u_18bitregister_3 (
    .\input (in_4), .clock(clk), .\output (n18bitregister_3_output), .enable(and_14_out));
  _18BitRegister u_18bitregister_4 (
    .\input (in_4), .clock(clk), .\output (n18bitregister_4_output), .enable(and_15_out));
  _18BitRegister u_18bitregister_5 (
    .\input (in_4), .clock(clk), .\output (n18bitregister_5_output), .enable(and_16_out));
  _18BitRegister u_18bitregister_6 (
    .\input (in_4), .clock(clk), .\output (n18bitregister_6_output), .enable(and_9_out));
  _18BitRegister u_18bitregister_7 (
    .\input (in_4), .clock(clk), .\output (n18bitregister_7_output), .enable(and_10_out));
  _18BitRegister u_18bitregister_8 (
    .\input (in_4), .clock(clk), .\output (n18bitregister_8_output), .enable(and_11_out));
  _18BitRegister u_18bitregister_9 (
    .\input (in_4), .clock(clk), .\output (n18bitregister_9_output), .enable(and_7_out));
  _18BitRegister u_18bitregister_10 (
    .\input (in_4), .clock(clk), .\output (n18bitregister_10_output), .enable(and_8_out));
  _18BitRegister u_18bitregister_11 (
    .\input (in_4), .clock(clk), .\output (n18bitregister_11_output), .enable(and_3_out));
  _18BitRegister u_18bitregister_12 (
    .\input (in_4), .clock(clk), .\output (n18bitregister_12_output), .enable(and_4_out));
  _18BitRegister u_18bitregister_13 (
    .\input (in_4), .clock(clk), .\output (n18bitregister_13_output), .enable(and_5_out));
  _18BitRegister u_18bitregister_14 (
    .\input (in_4), .clock(clk), .\output (n18bitregister_14_output), .enable(and_6_out));
  _18BitRegister u_18bitregister_15 (
    .\input (in_4), .clock(clk), .\output (n18bitregister_15_output), .enable(and_1_out));
  _18BitRegister u_18bitregister_16 (
    .\input (in_4), .clock(clk), .\output (n18bitregister_16_output), .enable(and_2_out));
  assign Register_1_Output = decoder_3_out13 ? n18bitregister_14_output : 18'bz;  // Controlled_Buffer controlled_buffer_1
  assign Register_2_Output = decoder_1_out13 ? n18bitregister_14_output : 18'bz;  // Controlled_Buffer controlled_buffer_2
  assign Register_1_Output = decoder_3_out14 ? n18bitregister_15_output : 18'bz;  // Controlled_Buffer controlled_buffer_3
  assign Register_2_Output = decoder_1_out14 ? n18bitregister_15_output : 18'bz;  // Controlled_Buffer controlled_buffer_4
  assign Register_1_Output = decoder_3_out15 ? n18bitregister_16_output : 18'bz;  // Controlled_Buffer controlled_buffer_5
  assign Register_2_Output = decoder_1_out15 ? n18bitregister_16_output : 18'bz;  // Controlled_Buffer controlled_buffer_6
  assign Register_1_Output = decoder_3_out9 ? n18bitregister_10_output : 18'bz;  // Controlled_Buffer controlled_buffer_7
  assign Register_2_Output = decoder_1_out9 ? n18bitregister_10_output : 18'bz;  // Controlled_Buffer controlled_buffer_8
  assign Register_1_Output = decoder_3_out10 ? n18bitregister_11_output : 18'bz;  // Controlled_Buffer controlled_buffer_9
  assign Register_2_Output = decoder_1_out10 ? n18bitregister_11_output : 18'bz;  // Controlled_Buffer controlled_buffer_10
  assign Register_1_Output = decoder_3_out11 ? n18bitregister_12_output : 18'bz;  // Controlled_Buffer controlled_buffer_11
  assign Register_2_Output = decoder_1_out11 ? n18bitregister_12_output : 18'bz;  // Controlled_Buffer controlled_buffer_12
  assign Register_1_Output = decoder_3_out12 ? n18bitregister_13_output : 18'bz;  // Controlled_Buffer controlled_buffer_13
  assign Register_2_Output = decoder_1_out12 ? n18bitregister_13_output : 18'bz;  // Controlled_Buffer controlled_buffer_14
  assign Register_1_Output = decoder_3_out5 ? n18bitregister_6_output : 18'bz;  // Controlled_Buffer controlled_buffer_15
  assign Register_2_Output = decoder_1_out5 ? n18bitregister_6_output : 18'bz;  // Controlled_Buffer controlled_buffer_16
  assign Register_1_Output = decoder_3_out6 ? n18bitregister_7_output : 18'bz;  // Controlled_Buffer controlled_buffer_17
  assign Register_2_Output = decoder_1_out6 ? n18bitregister_7_output : 18'bz;  // Controlled_Buffer controlled_buffer_18
  assign Register_1_Output = decoder_3_out7 ? n18bitregister_8_output : 18'bz;  // Controlled_Buffer controlled_buffer_19
  assign Register_2_Output = decoder_1_out7 ? n18bitregister_8_output : 18'bz;  // Controlled_Buffer controlled_buffer_20
  assign Register_1_Output = decoder_3_out8 ? n18bitregister_9_output : 18'bz;  // Controlled_Buffer controlled_buffer_21
  assign Register_2_Output = decoder_1_out8 ? n18bitregister_9_output : 18'bz;  // Controlled_Buffer controlled_buffer_22
  assign Register_1_Output = decoder_3_out1 ? n18bitregister_2_output : 18'bz;  // Controlled_Buffer controlled_buffer_23
  assign Register_2_Output = decoder_1_out1 ? n18bitregister_2_output : 18'bz;  // Controlled_Buffer controlled_buffer_24
  assign Register_1_Output = decoder_3_out2 ? n18bitregister_3_output : 18'bz;  // Controlled_Buffer controlled_buffer_25
  assign Register_2_Output = decoder_1_out2 ? n18bitregister_3_output : 18'bz;  // Controlled_Buffer controlled_buffer_26
  assign Register_1_Output = decoder_3_out3 ? n18bitregister_4_output : 18'bz;  // Controlled_Buffer controlled_buffer_27
  assign Register_2_Output = decoder_1_out3 ? n18bitregister_4_output : 18'bz;  // Controlled_Buffer controlled_buffer_28
  assign Register_1_Output = decoder_3_out4 ? n18bitregister_5_output : 18'bz;  // Controlled_Buffer controlled_buffer_29
  assign Register_2_Output = decoder_1_out4 ? n18bitregister_5_output : 18'bz;  // Controlled_Buffer controlled_buffer_30
  assign Register_1_Output = decoder_3_out0 ? n18bitregister_1_output : 18'bz;  // Controlled_Buffer controlled_buffer_31
  assign Register_2_Output = decoder_1_out0 ? n18bitregister_1_output : 18'bz;  // Controlled_Buffer controlled_buffer_32
endmodule

module _18BitRegister (
  input  [17:0] \input ,
  input  clock,
  input  enable,
  output [17:0] \output 
);

  DFlipFlop dflipflop_1 (.D(\input [0]), .clk(clock), .enable(enable), .Q(\output [0]));
  DFlipFlop dflipflop_2 (.D(\input [1]), .clk(clock), .enable(enable), .Q(\output [1]));
  DFlipFlop dflipflop_3 (.D(\input [2]), .clk(clock), .enable(enable), .Q(\output [2]));
  DFlipFlop dflipflop_4 (.D(\input [3]), .clk(clock), .enable(enable), .Q(\output [3]));
  DFlipFlop dflipflop_5 (.D(\input [4]), .clk(clock), .enable(enable), .Q(\output [4]));
  DFlipFlop dflipflop_6 (.D(\input [5]), .clk(clock), .enable(enable), .Q(\output [5]));
  DFlipFlop dflipflop_7 (.D(\input [6]), .clk(clock), .enable(enable), .Q(\output [6]));
  DFlipFlop dflipflop_8 (.D(\input [7]), .clk(clock), .enable(enable), .Q(\output [7]));
  DFlipFlop dflipflop_9 (.D(\input [8]), .clk(clock), .enable(enable), .Q(\output [8]));
  DFlipFlop dflipflop_10 (.D(\input [9]), .clk(clock), .enable(enable), .Q(\output [9]));
  DFlipFlop dflipflop_11 (.D(\input [10]), .clk(clock), .enable(enable), .Q(\output [10]));
  DFlipFlop dflipflop_12 (.D(\input [11]), .clk(clock), .enable(enable), .Q(\output [11]));
  DFlipFlop dflipflop_13 (.D(\input [12]), .clk(clock), .enable(enable), .Q(\output [12]));
  DFlipFlop dflipflop_14 (.D(\input [13]), .clk(clock), .enable(enable), .Q(\output [13]));
  DFlipFlop dflipflop_15 (.D(\input [14]), .clk(clock), .enable(enable), .Q(\output [14]));
  DFlipFlop dflipflop_16 (.D(\input [15]), .clk(clock), .enable(enable), .Q(\output [15]));
  DFlipFlop dflipflop_17 (.D(\input [16]), .clk(clock), .enable(enable), .Q(\output [16]));
  DFlipFlop dflipflop_18 (.D(\input [17]), .clk(clock), .enable(enable), .Q(\output [17]));
endmodule

module DLatch (
  input  D,
  input  enable,
  output Q
);

  wire nand_1_out, nand_2_out, nand_4_out, not_1_out;

  not not_1 (not_1_out, D);
  nand nand_1 (nand_1_out, D, enable);
  nand nand_2 (nand_2_out, enable, not_1_out);
  nand nand_3 (Q, nand_1_out, nand_4_out);
  nand nand_4 (nand_4_out, Q, nand_2_out);
endmodule

module DFlipFlop (
  input  D,
  input  clk,
  input  enable,
  output Q
);

  wire and_1_out, and_2_out, Master_q, not_1_out, not_2_out;

  not not_1 (not_1_out, clk);
  and and_1 (and_1_out, not_1_out, enable);
  not not_2 (not_2_out, not_1_out);
  and and_2 (and_2_out, not_2_out, enable);
  DLatch Master (.D(D), .Q(Master_q), .enable(and_1_out));
  DLatch Slave (.D(Master_q), .Q(Q), .enable(and_2_out));
endmodule

module Substractor (
  input  [17:0] in_1,
  input  [17:0] in_2,
  output [17:0] out_3,
  output CF
);

  wire n18bitadder_1_cout;
  wire [17:0] not_1_out;

  assign not_1_out = ~in_2;  // NOT_Gate not_1, 18 bits wide
  _18BitAdder u_18bitadder_1 (.cin(1'b1), .A(in_1), .B(not_1_out), .cout(n18bitadder_1_cout), .out_4(out_3));
  not not_2 (CF, n18bitadder_1_cout);
endmodule

module _18BitAdder (
  input  cin,
  input  [17:0] A,
  input  [17:0] B,
  output [17:0] out_4,
  output cout
);

  wire n2bitadder_1_cout, n2bitadder_2_cout, n2bitadder_3_cout, n2bitadder_4_cout, n2bitadder_5_cout,
       n2bitadder_6_cout, n2bitadder_7_cout, n2bitadder_8_cout;

  _2BitAdder u_2bitadder_1 (.cin(cin), .A(A[1:0]), .B(B[1:0]), .out_4(out_4[1:0]), .cout(n2bitadder_1_cout));
  _2BitAdder u_2bitadder_2 (
    .cin(n2bitadder_1_cout), .A(A[3:2]), .B(B[3:2]), .out_4(out_4[3:2]), .cout(n2bitadder_2_cout));
  _2BitAdder u_2bitadder_3 (
    .cin(n2bitadder_2_cout), .A(A[5:4]), .B(B[5:4]), .out_4(out_4[5:4]), .cout(n2bitadder_3_cout));
  _2BitAdder u_2bitadder_4 (
    .cin(n2bitadder_3_cout), .A(A[7:6]), .B(B[7:6]), .out_4(out_4[7:6]), .cout(n2bitadder_4_cout));
  _2BitAdder u_2bitadder_5 (
    .cin(n2bitadder_4_cout), .A(A[9:8]), .B(B[9:8]), .out_4(out_4[9:8]), .cout(n2bitadder_5_cout));
  _2BitAdder u_2bitadder_6 (
    .cin(n2bitadder_5_cout), .A(A[11:10]), .B(B[11:10]), .out_4(out_4[11:10]), .cout(n2bitadder_6_cout));
  _2BitAdder u_2bitadder_7 (
    .cin(n2bitadder_6_cout), .A(A[13:12]), .B(B[13:12]), .out_4(out_4[13:12]), .cout(n2bitadder_7_cout));
  _2BitAdder u_2bitadder_8 (
    .cin(n2bitadder_7_cout), .A(A[15:14]), .B(B[15:14]), .out_4(out_4[15:14]), .cout(n2bitadder_8_cout));
  _2BitAdder u_2bitadder_9 (.cin(n2bitadder_8_cout), .A(A[17:16]), .B(B[17:16]), .out_4(out_4[17:16]), .cout(cout));
endmodule

module _2BitAdder (
  input  cin,
  input  [1:0] A,
  input  [1:0] B,
  output [1:0] out_4,
  output cout
);

  wire n1bitadder_1_cout;

  _1BitAdder u_1bitadder_1 (.A(A[0]), .B(B[0]), .cin(cin), .sum(out_4[0]), .cout(n1bitadder_1_cout));
  _1BitAdder u_1bitadder_2 (.A(A[1]), .B(B[1]), .cin(n1bitadder_1_cout), .sum(out_4[1]), .cout(cout));

  // Notes on the sheet:
  //   cin: pull=up
endmodule

module _1BitAdder (
  input  A,
  input  B,
  input  cin,
  output sum,
  output cout
);

  wire and_1_out, and_2_out, xor_1_out;

  xor xor_1 (xor_1_out, A, B);
  and and_1 (and_1_out, B, A);
  xor xor_2 (sum, xor_1_out, cin);
  and and_2 (and_2_out, cin, xor_1_out);
  or or_1 (cout, and_2_out, and_1_out);
endmodule

module SignExtent6 (
  input  [17:0] in_1,
  output [17:0] out_2
);


  assign out_2 = {{13{in_1[5]}}, in_1[4:0]};
endmodule

module SignExtent14 (
  input  [17:0] in_1,
  output [17:0] out_2
);


  assign out_2 = {{5{in_1[13]}}, in_1[12:0]};
endmodule

module _18BitNORGate (
  input  [17:0] in_1,
  output out_2
);

  nor nor_1 (out_2, in_1[0], in_1[1], in_1[2], in_1[3], in_1[4], in_1[5], in_1[6], in_1[7], in_1[8], in_1[10], in_1[11], in_1[12], in_1[13], in_1[14], in_1[15], in_1[16], in_1[17], in_1[9]);
endmodule
